# Fritzing sketch Temp Sensor Boot innen (saved by Fritzing 0.9.4)

parts:
  Bauteil1 = Arduino Pro Mini v13
  DS1 = DS18B20 1-Wire Temperature Sensor [part_number=DS18B20]
  DS2 = DS18B20 1-Wire Temperature Sensor [part_number=DS18B20]
  DS3 = DS18B20 1-Wire Temperature Sensor [part_number=DS18B20]
  DS4 = DS18B20 1-Wire Temperature Sensor [part_number=DS18B20]
  LCD1 = LCD screen
  LCM1602_IIC1 = LCM1602 IIC [part_number="LCM1602 IIC" chip_label="LCM1602 IIC" package="DIP (Dual Inline) [THT]"]
  U1 = LM2596-Step-Down-Converter [package=THT]
  J1 = Piezo Speaker
  R4 = Resistor [tolerance=±5% resistance=10k package="0402 [SMD]"]
  R5 = Resistor [tolerance=±5% resistance=4.7k package="0402 [SMD]"]
  R6 = Resistor [tolerance=±5% resistance=10k package="0402 [SMD]"]
  R7 = Resistor [tolerance=±5% resistance=4.7k package="0402 [SMD]"]
  R3 = Resistor [tolerance=±5% resistance=4.7k package="0402 [SMD]"]
  R8 = Photocell (LDR) [package=THT]
  R9 = Resistor [tolerance=±5% resistance=1k package="0402 [SMD]"]
  R12 = Resistor [tolerance=±5% resistance=220 package="0402 [SMD]"]

nets:
  N1: Bauteil1.A4, R6.Pin_1, R7.Pin_0
  N2: Bauteil1.A5, R4.Pin_1, R5.Pin_0
  VDD: Bauteil1.RAW, DS1.VDD, DS2.VDD, DS3.VDD, DS4.VDD, LCM1602_IIC1.VCC, U1.pin3, R8.pin_1
  GND: Bauteil1.GND, DS1.GND, DS2.GND, DS3.GND, DS4.GND, LCM1602_IIC1.GND, U1.pin4, J1.pin1, R4.Pin_0, R6.Pin_0, R9.Pin_0
  N3: Bauteil1.VCC, R3.Pin_1
  N4: Bauteil1.A0, R8.pin_0, R9.Pin_1
  N5: Bauteil1.D9_PWM, R12.Pin_0
  N6: Bauteil1.D4, J1.pin2
  N7: Bauteil1.D3_PWM, DS1.DQ, DS2.DQ, DS3.DQ, DS4.DQ, R3.Pin_0
  VSS: LCD1.VSS, LCM1602_IIC1.VSS
  VDD_2: LCD1.VDD, LCM1602_IIC1.VDD
  N8: LCD1.V0, LCM1602_IIC1.V0
  N9: LCD1.RS, LCM1602_IIC1.RS
  N10: LCD1.R/W, LCM1602_IIC1.RW
  N11: LCD1.E, LCM1602_IIC1.E
  N12: LCD1.DB0, LCM1602_IIC1.D0
  N13: LCD1.DB1, LCM1602_IIC1.D1
  N14: LCD1.DB2, LCM1602_IIC1.D2
  N15: LCD1.DB3, LCM1602_IIC1.D3
  N16: LCD1.DB4, LCM1602_IIC1.D4
  N17: LCD1.DB5, LCM1602_IIC1.D5
  N18: LCD1.DB6, LCM1602_IIC1.D6
  N19: LCD1.DB7, LCM1602_IIC1.D7
  N20: LCD1.LED-, LCM1602_IIC1.A
  N21: LCD1.LED+, LCM1602_IIC1.K
  N22: LCM1602_IIC1.SDA, R7.Pin_1
  N23: LCM1602_IIC1.SCL, R5.Pin_1

notes:
  Motorraum
  5,0V
  4,7k
  Arduino mini pro (3,3V)
  4-fach Temp Anzeige für Boot
  Auspuff
  Seewasser
  LCD 4x20
  D-Lager
  12V in
  DS1820B
  Beeper
  2 x 4,7k
  2 x 10k
  1k
  LDR
  Damit wird das Display gedimmt
  Pin 7 vom U1 entlöten.
  Diese Leitung an die Basis von Q1 anlöten
  220

custom parts:
  LCD screen: A standard character display, usually with 2x16 characters. Comes in many colors.
  LCM1602 IIC: I2C-Module to use a 1602 or 2004 LCD on with the wire.h libory Serial LCD Modul
  LM2596-Step-Down-Converter: A dummy, proxy, ersatz, stand-in part for whatever you want. With 4 pins on a 100 mil inline pin header footprint.
